# Fritzing sketch ard-uno-with-op-amp (saved by Fritzing 0.9.3b)
breadboards: 1

parts:
  Part1 = Arduino Uno (Rev3)
  R2 = Resistor [tolerance=±1% resistance=1k package=THT]
  R3 = Resistor [tolerance=±1% resistance=3.3k package=THT]
  R4 = Resistor [tolerance=±1% resistance=1M package=THT]
  R5 = Resistor [tolerance=±1% resistance=330k package=THT]
  R6 = Resistor [tolerance=±1% resistance=100k package=THT]
  R7 = Resistor [tolerance=±1% resistance=33k package=THT]
  R8 = Resistor [tolerance=±1% resistance=10k package=THT]
  R10 = Resistor [tolerance=±5% resistance=100 package=THT]
  R11 = Resistor [tolerance=±5% resistance=1k package=THT]
  R12 = Resistor [tolerance=±5% resistance=10k package=THT]
  R13 = Resistor [tolerance=±5% resistance=100k package=THT]
  IC1 = 2 MHz rail-to-rail Op Amp [part_number=MCP6273 package="DIP (Dual Inline) [THT]"]
  R14 = Resistor [tolerance=±1% resistance=10M package=THT]

nets:
  N1: Part1.A4/SDA, IC1.Vin-, IC1.Vout
  N2: Part1.D8, R6.Pin_1
  N3: Part1.D9_PWM, R5.Pin_1
  N4: Part1.D10_PWM/SS, R4.Pin_1
  N5: Part1.D11_PWM/MOSI, R14.Pin_1
  GND: Part1.GND, R10.Pin_1, IC1.Vss, IC1.~CS
  N6: Part1.D4, R2.Pin_1
  N7: Part1.D5_PWM, R3.Pin_1
  N8: Part1.D6_PWM, R8.Pin_1
  N9: Part1.D7, R7.Pin_1
  5V: Part1.5V, IC1.Vdd
  N10: R2.Pin_0, R3.Pin_0, R4.Pin_0, R5.Pin_0, R6.Pin_0, R7.Pin_0, R8.Pin_0, R10.Pin_0, R11.Pin_0, R12.Pin_0, R13.Pin_0, IC1.Vin+, R14.Pin_0

notes:
  resistor(s) under test
  known resistors (1%)

custom parts:
  2 MHz rail-to-rail Op Amp: Single-supply rail-to-rail op amp. Datasheet: http://ww1.microchip.com/downloads/en/DeviceDoc/21810f.pdf
