# Fritzing sketch ard-uno (saved by Fritzing 0.9.3b)
breadboards: 1

parts:
  Part1 = Arduino Uno (Rev3)
  R1 = Resistor [tolerance=±5% resistance=150 package=THT]
  R2 = Resistor [tolerance=±5% resistance=1k package=THT]

nets:
  N1: Part1.A5/SCL, R1.Pin_0, R2.Pin_0
  N2: Part1.D11_PWM/MOSI, R2.Pin_1
  N3: Part1.D12/MISO, R1.Pin_1
